# Fritzing sketch Button (saved by Fritzing 0.9.3b)
breadboards: 1

parts:
  Componente1 = Arduino Uno (Rev3)
  D1 = Rectifier Diode [part_number=1N4001 package="300 mil [THT]"]
  D2 = Rectifier Diode [part_number=1N4001 package="300 mil [THT]"]
  R1 = Resistor [tolerance=±5% resistance=10k package=THT]
  R2 = Resistor [tolerance=±5% resistance=220 package=THT]
  LED1 = LED - 5mm [color="Red (633nm)" package="5 mm [THT]"]
  S1 = Pushbutton [package="[THT]"]
  R3 = Resistor [tolerance=±5% resistance=1k package=THT]
  R4 = Resistor [tolerance=±5% resistance=220 package=THT]
  LED2 = LED - 5mm [color="Red (633nm)" package="5 mm [THT]"]

nets:
  N1: Componente1.D4, R2.Pin_1, LED1.anode, S1.Pin_3, S1.Pin_4, R3.Pin_0
  N2: Componente1.D5_PWM, LED2.anode
  N3: Componente1.5V, D1.cathode, R1.Pin_0, R3.Pin_1
  N4: D1.anode, D2.cathode, R1.Pin_1, R2.Pin_0
  N5: D2.anode, LED1.cathode, S1.Pin_1, S1.Pin_2, R4.Pin_0
  N6: R4.Pin_1, LED2.cathode
