# Fritzing sketch RC_Filter (saved by Fritzing 0.9.3b)
breadboards: 1

parts:
  Componente1 = Arduino Uno (Rev3)
  R1 = Resistor [tolerance=±5% resistance=100k package=THT]
  C1 = Electrolytic Capacitor [capacitance=10µF package="100 mil [THT, electrolytic]"]

nets:
  N1: Componente1.A0, R1.Pin_1, C1.+
  N2: Componente1.A1, Componente1.D2, R1.Pin_0
  N3: Componente1.GND, C1.-
